# Fritzing sketch Project 2 Sketch (saved by Fritzing 0.9.3b)
breadboards: 1

parts:
  U1 = ESP32S-HiLetgo [part_number=ESP32S-HiLetgo]
  LED1 = LED - 5mm [color="Red (633nm)" package="5 mm [THT]"]
  LED2 = LED - 5mm [color="Yellow (592nm)" package="5 mm [THT]"]
  LED3 = LED - 5mm [color="Green (560nm)" package="5 mm [THT]"]
  R1 = Resistor [tolerance=±5% resistance=22 package=THT]
  R2 = Resistor [tolerance=±5% resistance=22 package=THT]
  R3 = Resistor [tolerance=±5% resistance=22 package=THT]
  S1 = Pushbutton [package="[THT]"]
  R4 = Resistor [tolerance=±5% resistance=220 package=THT]
  DHT1 = DHT11 Humitidy and Temperature Sensor (3 pins)

nets:
  N1: U1.3.3, S1.Pin_1, S1.Pin_2, R4.Pin_0
  N2: U1.GPIO36, S1.Pin_3, S1.Pin_4, R4.Pin_1
  GND: U1.GND, R1.Pin_0, R2.Pin_0, R3.Pin_0, DHT1.GND
  N3: U1.GPIO4, LED3.anode
  N4: U1.GPIO16, LED1.anode
  N5: U1.GPIO17, LED2.anode
  N6: LED1.cathode, R1.Pin_1
  N7: LED2.cathode, R2.Pin_1
  N8: LED3.cathode, R3.Pin_1

custom parts:
  ESP32S-HiLetgo: HiLetgo ESP-WROOM-32 ESP32 ESP-32S Development Board 2.4GHz Dual-Mode WiFi + Bluetooth Dual Cores Microcontroller The ESP32 integrated with Antenna switches, RF Balun, power amplifiers, low-noise amplifiers, filters, and management modules, and the entire solution occupies the least area of PCB. 2.4 GHz Wi-Fi plus Bluetooth dual-mode chip, with TSMC Ultra-low power consumption 40nm technology,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
  DHT11 Humitidy and Temperature Sensor (3 pins): DHT11 Humidity and Temperature Sensor (3 pins) from the design created by John De Cristofaro for Adafruit Industries.
