# Fritzing sketch Project 3 Sketch (saved by Fritzing 0.9.3b)
breadboards: 1

parts:
  DHT1 = DHT11 Humitidy and Temperature Sensor (3 pins)
  R1 = Photocell (LDR) [package=THT]
  LED1 = LED - 5mm [color="Red (633nm)" package="5 mm [THT]"]
  LED2 = LED - 5mm [color="Green (570nm)" package="5 mm [THT]"]
  LED3 = LED - 5mm [color="Red (633nm)" package="5 mm [THT]"]
  LED4 = LED - 5mm [color="Green (570nm)" package="5 mm [THT]"]
  R3 = Resistor [tolerance=±5% resistance=180 package=THT]
  R2 = Resistor [tolerance=±5% resistance=4.7k package=THT]
  R4 = Resistor [tolerance=±5% resistance=180 package=THT]
  R5 = Resistor [tolerance=±5% resistance=180 package=THT]
  R6 = Resistor [tolerance=±5% resistance=180 package=THT]
  U1 = ESP32S-HiLetgo [part_number=ESP32S-HiLetgo]

nets:
  N1: DHT1.DATA, U1.GPIO32
  N2: DHT1.VDD, R1.pin_1, U1.3.3
  GND: DHT1.GND, R3.Pin_0, R2.Pin_0, R4.Pin_0, R5.Pin_0, R6.Pin_0, U1.GND
  N3: R1.pin_0, R2.Pin_1, U1.GPIO36
  N4: LED1.anode, U1.GPIO4
  N5: LED2.anode, U1.GPIO16
  N6: LED3.anode, U1.GPIO17
  N7: LED4.anode, U1.GPIO33

custom parts:
  DHT11 Humitidy and Temperature Sensor (3 pins): DHT11 Humidity and Temperature Sensor (3 pins) from the design created by John De Cristofaro for Adafruit Industries.
  ESP32S-HiLetgo: HiLetgo ESP-WROOM-32 ESP32 ESP-32S Development Board 2.4GHz Dual-Mode WiFi + Bluetooth Dual Cores Microcontroller The ESP32 integrated with Antenna switches, RF Balun, power amplifiers, low-noise amplifiers, filters, and management modules, and the entire solution occupies the least area of PCB. 2.4 GHz Wi-Fi plus Bluetooth dual-mode chip, with TSMC Ultra-low power consumption 40nm technology,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
